# Fritzing sketch sketch (saved by Fritzing 0.9.4)

parts:
  Part1 = Arduino Micro (Rev3)  # not connected
  Raspberry_Pi_1 = Raspberry Pi 3 [part_number=RPI-3-V1.2]
  IC1 = IC, DIP package, 8 pins [chip_label=MCP]
  M1 = RioRand LM2596
  U1 = LCD_CFAX [package=lcd_cfax]  # not connected
  J1 = JST-B3P-VH [part_number=JST-B3P-VH package=THT]  # not connected

nets:
  N1: Raspberry_Pi_1.GND, M1.Pin_4
  N2: Raspberry_Pi_1.5V, M1.Pin_3
  N3: IC1.pin1, M1.Pin_2
  N4: IC1.pin3, M1.Pin_1

notes:
  CAR LIN
  CAR GND
  CAR 12V
  USB Smartphone
  5V
  RTI module connector serial
  Simplified RTI display
  USB cable
